# Fritzing sketch ECU monitor (saved by Fritzing 0.9.3b)
breadboards: 2

parts:
  U1 = Voltage Regulator - 8V [part_number=L7808CV package="TO220 [THT]"]
  Part1 = Arduino Nano (Rev3.0)
  R1 = Resistor [tolerance=±5% resistance=56k package=THT]
  R2 = Resistor [tolerance=±5% resistance=12k package=THT]
  Q1 = NPN-Transistor [package="TO92 [THT]"]
  R17 = Resistor [tolerance=±5% resistance=1k package="1206 [SMD]"]
  R18 = Resistor [tolerance=±5% resistance=1k package="1206 [SMD]"]
  X1 = F25 [package=db25]
  R3 = Resistor [tolerance=±5% resistance=5.6k package=THT]
  D2 = Zener Diode [part_number=1N4732A breakdown_voltage=4.7V package="300 mil [THT]"]
  R20 = Resistor [tolerance=±5% resistance=3.3k package=THT]
  J1 = Camdenboss CTB0158-3 [part_number=CTB0158-3 package=THT]
  J2 = Camdenboss CTB0158-2 [part_number=CTB0158-2 package=THT]
  R21 = Resistor [tolerance=±5% resistance=56 package=THT]
  R22 = Resistor [tolerance=±5% resistance=47 package=THT]
  R23 = Resistor [tolerance=±5% resistance=3.3k package=THT]
  R24 = Resistor [tolerance=±5% resistance=3.3k package=THT]
  D3 = Zener Diode [part_number=1N4732A breakdown_voltage=4.7V package="300 mil [THT]"]
  D4 = Zener Diode [part_number=1N4732A breakdown_voltage=4.7V package="300 mil [THT]"]
  R25 = Resistor [tolerance=±5% resistance=5.6k package=THT]
  R26 = Resistor [tolerance=±5% resistance=5.6k package=THT]
  R19 = Resistor [tolerance=±5% resistance=27k package=THT]
  D1 = Diode [part_number=1N4007 package=diode-1n4001]
  C1 = Ceramic Capacitor [capacitance=100nF package="100 mil [THT, multilayer]"]
  C2 = Ceramic Capacitor [capacitance=100nF package="100 mil [THT, multilayer]"]

nets:
  N1: U1.input_voltage, D1.C, C1.0
  GND: U1.GND, Part1.GND, R2.Pin_1, Q1.E, X1.13, D2.anode, J2.pin2, D3.anode, D4.anode, C1.1, C2.0
  8V: U1.output_voltage, Part1.VIN, C2.1
  N2: Part1.D2, R20.Pin_0
  throttle sw: Part1.D4, X1.11
  N3: Part1.D9, R23.Pin_0
  N4: Part1.D10, R24.Pin_0
  N5: Part1.D12/MISO, R18.Pin_0
  N6: Part1.5V, R21.Pin_0, R22.Pin_0, R19.Pin_0
  fuel level: Part1.A6, J2.pin1, R21.Pin_1
  oil pressure: Part1.A5, J1.pin1, R22.Pin_1
  ECT: Part1.A4, X1.10
  IAT: Part1.A3, X1.9
  air flow meter: Part1.A2, X1.21
  oxygen sensor: Part1.A1, X1.2
  N7: Part1.A0, R1.Pin_1, R2.Pin_0
  diagnostics: Part1.D13/SCK, Q1.C, R17.Pin_0, X1.20
  power: R1.Pin_0, R17.Pin_1, X1.14, D1.A
  N8: Q1.B, R18.Pin_1
  start signal: X1.1, R3.Pin_1
  fuel pump: X1.3
  sensor GND: X1.6
  hall power: X1.8
  injectors: X1.12
  sensor power: X1.17
  hall sensor: X1.18
  engine GND: X1.19
  rpm signal: X1.24
  ignition: X1.25
  N9: R3.Pin_0, D2.cathode, R20.Pin_1, R19.Pin_1
  oil pressure sw1: J1.pin2, R26.Pin_1
  oil pressure sw2: J1.pin3, R25.Pin_1
  N10: R23.Pin_1, D3.cathode, R26.Pin_0
  N11: R24.Pin_1, D4.cathode, R25.Pin_0

custom parts:
  Voltage Regulator - 8V: 8V DC Voltage Regulator
